# Fritzing sketch Fritzing 1 (saved by Fritzing 0.9.4)
circuit board: 12.2678cm x 6.89412cm
breadboards: 1

parts:
  Componente1 = Arduino Mega ADK (Rev3)
  KYLE = Keyes Relay [package=THT]
  BLUETOOTH = Bluetooth HC-05 Macho

nets (from the schematic view):
  GND: Componente1.GND, KYLE.ground, BLUETOOTH.GND
  5V: Componente1.5V, KYLE.power, BLUETOOTH.VCC
  N1: Componente1.D0/RX0, BLUETOOTH.State, BLUETOOTH.TXD
  N2: Componente1.D1/TX0, BLUETOOTH.RXD
  N3: Componente1.D2_PWM, KYLE.signal
  N4: KYLE.NC, KYLE.C, KYLE.NO

custom parts:
  Keyes Relay: The Keyes 5V relay module is suitable for SCM development, home appliance control. It uses a 5V~12V TIL control signal which can control DC / AC signal.
