# Fritzing sketch PCB 3 (saved by Fritzing 0.9.4)
circuit board: 12.2584cm x 6.84795cm

parts:
  Componente2 = Arduino Mega ADK (Rev3)
  KY-1 = Keyes Relay [package=THT]
  Componente1 = Bluetooth HC-05 Macho

nets:
  GND: Componente2.GND, KY-1.ground, Componente1.GND
  5V: Componente2.IOREF, Componente2.5V, KY-1.power, Componente1.VCC
  N1: Componente2.D0/RX0, Componente1.TXD
  N2: Componente2.D1/TX0, Componente1.RXD
  N3: Componente2.D2_PWM, KY-1.signal

custom parts:
  Keyes Relay: The Keyes 5V relay module is suitable for SCM development, home appliance control. It uses a 5V~12V TIL control signal which can control DC / AC signal.
